# Fritzing sketch RFGatewaySchematic (saved by Fritzing 0.9.4)
breadboards: 1

parts:
  LED1 = LED - 5mm [color="Red (633nm)" package="5 mm [THT]"]
  LED2 = LED - 5mm [color="Green (570nm)" package="5 mm [THT]"]
  R1 = Resistor [tolerance=±5% resistance=100 package="0402 [SMD]"]
  R2 = Resistor [tolerance=±5% resistance=150 package="0402 [SMD]"]
  S2 = Toggle Switch [package=THT]
  J1 = Piezo Speaker
  Composant1 = Arduino Ethernet Shield (Rev3)
  U1 = RF-LINK_RX [package=rf-link_rx]
  U2 = RF-LINK_TX [package=rf-link_tx]
  ANT1 = Antenna
  ANT2 = Antenna

nets:
  N1: LED1.cathode, R2.Pin_1
  N2: LED1.anode, Composant1.D8
  N3: LED2.cathode, R1.Pin_1
  N4: LED2.anode, Composant1.D7
  GND: R1.Pin_0, R2.Pin_0, S2.COM, Composant1.GND, U1.GND, U2.GND
  N5: S2.L1, J1.pin1
  N6: J1.pin2, Composant1.PWM_D9
  N7: Composant1.PWM_D3, U2.DATA
  N8: Composant1.PWM_D5, U1.DATA
  +5V: Composant1.5V, U1.+5V, U2.+5V
  N9: U1.ANT, ANT2.antenna_lead
  N10: U2.ANT, ANT1.antenna_lead

notes:
  Gateway
