# Fritzing sketch RFStationSchematic (saved by Fritzing 0.9.4)
breadboards: 1

parts:
  U1 = RF-LINK_RX [package=rf-link_rx]
  U2 = RF-LINK_TX [package=rf-link_tx]
  ANT1 = Antenna
  ANT2 = Antenna
  Composant1 = Arduino Uno (Rev3) - ICSP

nets:
  GND: U1.GND, U2.GND, Composant1.GND
  N1: U1.DATA, Composant1.D5_PWM
  +5V: U1.+5V, U2.+5V, Composant1.5V
  N2: U1.ANT, ANT2.antenna_lead
  N3: U2.ANT, ANT1.antenna_lead
  N4: U2.DATA, Composant1.D3_PWM

notes:
  Station
